# Fritzing sketch DronePoles (saved by Fritzing 0.9.2b)
circuit board: 8.46667cm x 5.64444cm
breadboards: 1

parts:
  LED1 = RGB LED - (4 legs) [package="5 mm [THT]"]
  R2 = Resistor [tolerance=±5% resistance=220 package="2512 [SMD]"]
  R3 = Resistor [tolerance=±5% resistance=220 package="2512 [SMD]"]
  Part2 = SRF05 Ultrasonic Rangefinder
  Pro_Micro1 = Pro Micro
  BAT1 = BC9VPC [package=bc9vpc]
  R1 = Resistor [tolerance=±5% resistance=220 package="2512 [SMD]"]

nets:
  VCC: LED1.common_anode, Part2.VCC, Pro_Micro1.VCC
  N1: R2.Pin_0, Pro_Micro1.D6
  N2: R3.Pin_0, Pro_Micro1.D5
  N3: Part2.Trig, Pro_Micro1.D4
  N4: Part2.Echo, Pro_Micro1.D3
  N5: Part2.GND, Pro_Micro1.GND#3, BAT1.V-
  N6: Pro_Micro1.D9, R1.Pin_0
  N7: Pro_Micro1.D20/A2, Pro_Micro1.GND#23
  N8: Pro_Micro1.RAW, BAT1.V+

custom parts:
  Pro Micro: The SparkFun Pro Micro is a complete USB-based microcontoller development system, in a very small footprint, capable of implementing many types of projects. All programming can be done via the USB port.
